# Fritzing sketch noiseBoxSchematic (saved by Fritzing 0.9.3b)
breadboards: 1

parts:
  부품3 = Arduino Uno (Rev3)
  R6 = Resistor [tolerance=±5% resistance=330 package=THT]
  R7 = Resistor [tolerance=±5% resistance=10k package=THT]
  R8 = Resistor [tolerance=±5% resistance=330 package=THT]
  LED2 = LED - 5mm [color="Blue (430nm)" package="5 mm [THT]"]
  NEOPIXEL3 = Neopixel Strip -- Black (30/m)
  BUTTON3 = Arcade Button (blue)
  C2 = Electrolytic Capacitor [capacitance=1mF package="0807 [SMD, electrolytic]"]
  Power_plug4 = Power plug
  SCK_1_1 = Smart Citizen Kit 1.5
  R9 = Resistor [tolerance=±5% resistance=4.7k package=THT]
  R10 = Resistor [tolerance=±5% resistance=4.7k package=THT]

nets:
  N1: 부품3.A4/SDA, SCK_1_1.SDA, R9.Pin_1
  N2: 부품3.A5/SCL, SCK_1_1.SCL, R10.Pin_1
  N3: 부품3.D2, R7.Pin_1, BUTTON3.no_name_yet#1
  N4: 부품3.D3_PWM, R6.Pin_1
  N5: 부품3.D6_PWM, R8.Pin_1
  N6: 부품3.3V3, R9.Pin_0, R10.Pin_0
  5V: 부품3.5V, BUTTON3.no_name_yet#2, SCK_1_1.VCC
  GND: 부품3.GND, R7.Pin_0, LED2.cathode, NEOPIXEL3.GND, C2.-, Power_plug4.GND, SCK_1_1.GND
  N7: R6.Pin_0, LED2.anode
  N8: R8.Pin_0, NEOPIXEL3.DI
  +5V: NEOPIXEL3.+5V, C2.+, Power_plug4.VCC

custom parts:
  Neopixel Strip -- Black (30/m): Neopixel Strip, Black, 30 pixels per meter.
  Arcade Button (blue): Adafruit Arcade Button (blue)
  Smart Citizen Kit 1.5: Smart Citizen Kit 1.5 rev C
